# Fritzing sketch Schematic (saved by Fritzing 0.9.6b)
breadboards: 1

parts:
  S1 = Toggle Switch [package=THT]
  R1 = Resistor [tolerance=±5% power=0.25 resistance=220 package=THT]
  LED1 = LED - 5mm [color="Red (633nm)" current=0.030 package="5 mm [THT]"]  # not connected
  Raspberry_Pi_1 = Raspberry Pi 3 [part_number=RPI-3-V1.2]
  R2 = Resistor [tolerance=±5% resistance=220 package="2512 [SMD]"]  # not connected
  R3 = Resistor [tolerance=±5% power=0.25 resistance=220 package=THT]
  LED2 = LED - 5mm [color="Red (633nm)" current=0.030 package="5 mm [THT]"]  # not connected

nets:
  N1: S1.COM, Raspberry_Pi_1.GPIO20
  N2: R1.Pin_0, Raspberry_Pi_1.GPIO16
  N3: Raspberry_Pi_1.GPIO21, R3.Pin_0
